# Fritzing sketch Dolce-Gusto-Timer (saved by Fritzing 0.9.2b)
circuit board: 8.46667cm x 5.64444cm
breadboards: 1

parts:
  U2 = TTL UART CP2102
  2x_22_pF = Capacitor [part_number="(code 22 or 220)" package=cap-pth-small2]
  22pF1 = Capacitor [part_number="(code 22 or 220)" package=cap-pth-small2]
  0_10_uF = Capacitor [part_number="(code 104)" package=cap-pth-small2]
  R1 = Resistor [tolerance=±5% resistance=10k part_number=resistor package=THT]
  U3 = POT [package=pot_alpha_rv16af-20]
  U4 = 74HC595 [package="DIP16 [THT]"]
  16MHZ = CRYSTAL [part_number=crystal package=hc49u-v]
  J1 = Basic Servo
  R2 = Resistor [tolerance=±5% resistance=330 package="2512 [SMD]"]
  R3 = Resistor [tolerance=±5% resistance=330 package="2512 [SMD]"]
  R4 = Resistor [tolerance=±5% resistance=330 package="2512 [SMD]"]
  R5 = Resistor [tolerance=±5% resistance=330 package="2512 [SMD]"]
  R6 = Resistor [tolerance=±5% resistance=330 package="2512 [SMD]"]
  R7 = Resistor [tolerance=±5% resistance=330 package="2512 [SMD]"]
  R8 = Resistor [tolerance=±5% resistance=10k package="2512 [SMD]"]
  LED9 = LED - 3mm [color="Green (555nm)" package="3 mm [THT]"]
  LED10 = LED - 3mm [color="Green (555nm)" package="3 mm [THT]"]
  LED11 = LED - 3mm [color="Green (555nm)" package="3 mm [THT]"]
  LED12 = LED - 3mm [color="Green (555nm)" package="3 mm [THT]"]
  LED13 = LED - 3mm [color="Green (555nm)" package="3 mm [THT]"]
  LED14 = LED - 3mm [color="Green (555nm)" package="3 mm [THT]"]
  LED15 = LED - 3mm [color="Green (555nm)" package="3 mm [THT]"]
  U5 = atmega328 [package=dip]
  0_10_uF1 = Capacitor [part_number="(code 104)" package=cap-pth-small2]
  S1 = Pushbutton [package="[THT]"]
  R10 = Resistor [tolerance=±5% resistance=330 package="2512 [SMD]"]
  LED16 = LED - 3mm [color="Red (633nm)" package="3 mm [THT]"]

nets:
  N1: U2.DTR, 0_10_uF.1
  N2: U2.RXD, U5.D1_(TX)
  N3: U2.TXD, U5.D0_(RX)
  VCC: U2.+5V, R1.Pin_1, U3.E, U4.MR, J1.vcc, U5.VCC, S1.Pin_1, S1.Pin_2
  GND: U2.GND, 2x_22_pF.1, 22pF1.2, U3.A, U4.OE, J1.gnd, R8.Pin_0, LED9.cathode, LED10.cathode, LED11.cathode, LED12.cathode, LED13.cathode, LED14.cathode, LED15.cathode, U5.GND#7, 0_10_uF1.1, LED16.cathode
  N4: 2x_22_pF.2, 16MHZ.1, U5.XLAT2
  N5: 22pF1.1, 16MHZ.2, U5.XLAT1
  N6: 0_10_uF.2, R1.Pin_0, U5.RESET
  N7: U3.S, U5.A4
  N8: U4.Q1, R3.Pin_1
  N9: U4.Q2, R4.Pin_1
  N10: U4.Q3, R5.Pin_1
  N11: U4.Q4, R6.Pin_1
  N12: U4.Q5, R7.Pin_1
  N13: U4.SH_CP, U5.D12
  N14: U4.ST_CP, U5.D8, 0_10_uF1.2
  N15: U4.DS, U5.D11_(PWM)
  N16: U4.Q0, R2.Pin_1
  N17: J1.pulse, U5.D10_(PWM)
  N18: R2.Pin_0, LED15.anode
  N19: R3.Pin_0, LED14.anode
  N20: R4.Pin_0, LED13.anode
  N21: R5.Pin_0, LED12.anode
  N22: R6.Pin_0, LED11.anode
  N23: R7.Pin_0, LED10.anode
  N24: R8.Pin_1, U5.D2, S1.Pin_3, S1.Pin_4
  N25: U5.D3_(PWM), R10.Pin_0, R10.Pin_1, LED16.anode

custom parts:
  TTL UART CP2102: 6Pin USB 2.0 to TTL UART Module Serial Converter CP2102 STC Replace Ft232 Module
